# Fritzing sketch LED_Analog (saved by Fritzing 0.9.3b)
breadboards: 1

parts:
  LED1 = LED - 5mm [color="Red (633nm)" package="5 mm [THT]"]
  LED2 = LED - 5mm [color="Green (570nm)" package="5 mm [THT]"]
  부품1 = Arduino Uno (Rev3)
  R1 = Resistor [tolerance=±5% resistance=1k package=THT]
  S1 = Pushbutton [package="[THT]"]
  R2 = Resistor [tolerance=±5% resistance=1k package=THT]
  S2 = Pushbutton [package="[THT]"]

nets:
  N1: LED1.cathode, LED2.cathode, 부품1.GND, R1.Pin_0
  N2: LED1.anode, 부품1.D10_PWM/SS
  N3: LED2.anode, 부품1.D11_PWM/MOSI
  N4: 부품1.D5_PWM, R1.Pin_1, S1.Pin_3, S1.Pin_4
  N5: 부품1.D6_PWM, R2.Pin_1, S2.Pin_3, S2.Pin_4
  N6: 부품1.5V, S1.Pin_1, S1.Pin_2, R2.Pin_0, S2.Pin_1, S2.Pin_2
