# Fritzing sketch Servo_Button_bk (saved by Fritzing 0.9.3b)
circuit board: 8.8931cm x 5.78658cm
breadboards: 1

parts:
  부품1 = Arduino Uno (Rev3)
  S1 = Pushbutton [package="[THT]"]
  S2 = Pushbutton [package="[THT]"]
  R2 = Resistor [tolerance=±5% resistance=1k package=THT]
  J1 = Basic Servo
  R3 = Resistor [tolerance=±5% resistance=1k package=THT]

nets:
  GND: 부품1.GND, R2.Pin_1, J1.gnd, R3.Pin_1
  N1: 부품1.D3_PWM, J1.pulse
  N2: 부품1.D4, S1.Pin_1, S1.Pin_2, R2.Pin_0
  N3: 부품1.D5_PWM, S2.Pin_1, S2.Pin_2, R3.Pin_0
  5V: 부품1.5V, S1.Pin_3, S1.Pin_4, S2.Pin_3, S2.Pin_4, J1.vcc
