# Fritzing sketch Servo_CdS (saved by Fritzing 0.9.3b)
circuit board: 8.46667cm x 5.64444cm
breadboards: 1

parts:
  부품1 = Arduino Uno (Rev3)
  R1 = Resistor [tolerance=±5% resistance=1k package=THT]
  LED1 = LED - 5mm [color="Red (633nm)" package="5 mm [THT]"]
  R2 = Photocell (LDR) [package=THT]
  R3 = Resistor [tolerance=±5% resistance=220 package=THT]

nets:
  N1: 부품1.A0, R2.pin_1, R3.Pin_1
  N2: 부품1.GND, LED1.cathode, R2.pin_0
  N3: 부품1.D3_PWM, R1.Pin_0
  N4: 부품1.5V, R3.Pin_0
  N5: R1.Pin_1, LED1.anode
