# Fritzing sketch Servo_DynamicResistor (saved by Fritzing 0.9.3b)
circuit board: 8.46667cm x 5.64444cm
breadboards: 1

parts:
  부품1 = Arduino Uno (Rev3)
  R1 = Resistor [tolerance=±5% resistance=1k package=THT]
  LED1 = LED - 5mm [color="Red (633nm)" package="5 mm [THT]"]
  R4 = Rotary Potentiometer (Small) [maximum_resistance=100kΩ package=THT]

nets:
  N1: 부품1.A0, R4.wiper
  N2: 부품1.D3_PWM, R1.Pin_0
  N3: 부품1.5V, R4.leg1
  N4: 부품1.GND, LED1.cathode, R4.leg2
  N5: R1.Pin_1, LED1.anode
